# Fritzing sketch fotorezytor (saved by Fritzing 0.9.3b)
breadboards: 1

parts:
  R3 = Photocell (LDR) [package=THT]
  Part1 = Arduino Nano (Rev3.0)

nets:
  N1: R3.pin_0, Part1.A0
  N2: R3.pin_1, Part1.GND
