# Fritzing sketch fotorezytor_i_dioda (saved by Fritzing 0.9.3b)
breadboards: 1

parts:
  R3 = Photocell (LDR) [package=THT]
  Part1 = Arduino Nano (Rev3.0)
  LED1 = LED - 5mm [color="Red (633nm)" package="5 mm [THT]"]

nets:
  N1: R3.pin_0, Part1.A0
  N2: R3.pin_1, Part1.GND, LED1.cathode
  N3: Part1.D9, LED1.anode
