# Fritzing sketch fotorezytor_i_glosnik (saved by Fritzing 0.9.3b)
breadboards: 1

parts:
  R3 = Photocell (LDR) [package=THT]
  Part1 = Arduino Nano (Rev3.0)
  LED1 = LED - 5mm [color="Red (633nm)" package="5 mm [THT]"]
  J2 = Piezo Speaker

nets:
  N1: R3.pin_0, Part1.A0
  N2: R3.pin_1, Part1.GND, LED1.cathode, J2.pin1
  N3: Part1.D8, J2.pin2
  N4: Part1.D9, LED1.anode
