# Fritzing sketch przycisk (saved by Fritzing 0.9.3b)
breadboards: 1

parts:
  Part1 = Arduino Nano (Rev3.0)
  S2 = Pushbutton [package="[SMD]"]

nets:
  N1: Part1.GND, S2.Pin_3, S2.Pin_4
  N2: S2.Pin_1, S2.Pin_2
