# Fritzing sketch czujnik_odleglosci (saved by Fritzing 0.9.3b)
breadboards: 1

parts:
  Part1 = Arduino Nano (Rev3.0)
  HC-SR04_Sensor_1 = HC-SR04 Ultrasonic Distance Sensor

nets:
  N1: Part1.D11/MOSI, HC-SR04_Sensor_1.ECHO
  N2: Part1.D12/MISO, HC-SR04_Sensor_1.TRIG
  GND: Part1.GND, HC-SR04_Sensor_1.GND
  5V: Part1.5V, HC-SR04_Sensor_1.VCC
