# Fritzing sketch sonar_i_ledy (saved by Fritzing 0.9.3b)
breadboards: 1

parts:
  HC-SR04_Sensor_1 = HC-SR04 Ultrasonic Distance Sensor
  Part1 = Maker Uno (Arduino Uno Compatible)

nets:
  VCC: HC-SR04_Sensor_1.VCC, Part1.5V
  N1: HC-SR04_Sensor_1.TRIG, Part1.D12/MISO
  N2: HC-SR04_Sensor_1.ECHO, Part1.D11_PWM/MOSI
  GND: HC-SR04_Sensor_1.GND, Part1.GND

custom parts:
  Maker Uno (Arduino Uno Compatible): Maker Uno, an Arduino UNO compatible board designed and developed specially for students to learn coding and microcontroller. We named it Maker UNO to encourage everyone to be a maker by getting started with this amazing board. Oh! BTW, it is PURPLE color.
