# Fritzing sketch sonar_i_serwo (saved by Fritzing 0.9.3b)
breadboards: 1

parts:
  Part1 = Arduino Nano (Rev3.0)
  HC-SR04_Sensor_1 = HC-SR04 Ultrasonic Distance Sensor
  J2 = Basic Servo

nets:
  N1: Part1.D2, J2.pulse
  N2: Part1.D11/MOSI, HC-SR04_Sensor_1.ECHO
  N3: Part1.D12/MISO, HC-SR04_Sensor_1.TRIG
  GND: Part1.GND, HC-SR04_Sensor_1.GND, J2.gnd
  VCC: Part1.5V, HC-SR04_Sensor_1.VCC, J2.vcc
