# Fritzing sketch mikrofon (saved by Fritzing 0.9.4)

parts:
  Part1 = Maker Uno (Arduino Uno Compatible)
  Part2 = Breakout Board for Electret Microphone

nets:
  N1: Part1.A0, Part2.AUD
  5V: Part1.5V, Part2.VCC
  GND: Part1.GND, Part2.GND

custom parts:
  Maker Uno (Arduino Uno Compatible): Maker Uno, an Arduino UNO compatible board designed and developed specially for students to learn coding and microcontroller. We named it Maker UNO to encourage everyone to be a maker by getting started with this amazing board. Oh! BTW, it is PURPLE color.
