# Fritzing sketch mikrofonServo (saved by Fritzing 0.9.4)
breadboards: 1

parts:
  Part1 = Maker Uno (Arduino Uno Compatible)
  Part2 = Breakout Board for Electret Microphone
  J1 = Basic Servo

nets:
  N1: Part1.A0, Part2.AUD
  N2: Part1.D2, J1.pulse
  VCC: Part1.5V, Part2.VCC, J1.vcc
  GND: Part1.GND, Part2.GND, J1.gnd

custom parts:
  Maker Uno (Arduino Uno Compatible): Maker Uno, an Arduino UNO compatible board designed and developed specially for students to learn coding and microcontroller. We named it Maker UNO to encourage everyone to be a maker by getting started with this amazing board. Oh! BTW, it is PURPLE color.
