# Fritzing sketch e04_wedrowiecPokretlo (saved by Fritzing 0.9.3b)
breadboards: 1

parts:
  Part1 = Arduino Leonardo (Rev3b)
  U1 = POT [package=pot_mammoth]
  NEOPIXEL1 = Neopixel Strip -- White (60/m) [part_number=1138]

nets:
  N1: Part1.D6_PWM/A7, NEOPIXEL1.DI
  5V: Part1.5V, U1.S, NEOPIXEL1.+5V
  N2: Part1.A0, U1.A
  GND: Part1.GND, U1.E, NEOPIXEL1.GND

notes:
  BLINK

custom parts:
  Neopixel Strip -- White (60/m): Neopixel Strip, White, 60 pixels per meter.

// code stored in the sketch: Blink.ino
/*
  Blink
  
  Switching a LED on and off
  
  This example is part of the Fritzing Creator Kit: www.fritzing.org/creator-kit.
*/

int led = 13;                   // integer variable led is declared

void setup() {                  // the setup() method is executed only once
  pinMode(led, OUTPUT);         // the led PIN is declared as digital output
}

void loop() {                   // the loop() method is repeated
  digitalWrite(led, HIGH);      // switching on the led 
  delay(1000);                  // stopping the program for 1000 milliseconds
  digitalWrite(led, LOW);       // switching off the led 
  delay(1000);                  // stopping the program for 1000 milliseconds
}
