# Fritzing sketch e05_wedrowcyDwajFoto (saved by Fritzing 0.9.3b)
breadboards: 1

parts:
  Part1 = Arduino Leonardo (Rev3b)
  NEOPIXEL1 = Neopixel Strip -- White (60/m) [part_number=1138]
  R1 = Photocell (LDR) [package=THT]
  R2 = Photocell (LDR) [package=THT]

nets:
  N1: Part1.D6_PWM/A7, NEOPIXEL1.DI
  5V: Part1.5V, NEOPIXEL1.+5V
  N2: Part1.A0, R1.pin_1
  N3: Part1.A1, R2.pin_0
  GND: Part1.GND, NEOPIXEL1.GND, R1.pin_0, R2.pin_1

notes:
  BLINK

custom parts:
  Neopixel Strip -- White (60/m): Neopixel Strip, White, 60 pixels per meter.

// code stored in the sketch: Blink.ino
/*
  Blink
  
  Switching a LED on and off
  
  This example is part of the Fritzing Creator Kit: www.fritzing.org/creator-kit.
*/

int led = 13;                   // integer variable led is declared

void setup() {                  // the setup() method is executed only once
  pinMode(led, OUTPUT);         // the led PIN is declared as digital output
}

void loop() {                   // the loop() method is repeated
  digitalWrite(led, HIGH);      // switching on the led 
  delay(1000);                  // stopping the program for 1000 milliseconds
  digitalWrite(led, LOW);       // switching off the led 
  delay(1000);                  // stopping the program for 1000 milliseconds
}
