# Fritzing sketch przyciski (saved by Fritzing 0.9.3b)
breadboards: 1

parts:
  S9 = Pushbutton [package="[SMD]"]
  S10 = Pushbutton [package="[SMD]"]
  S11 = Pushbutton [package="[SMD]"]
  JP7 = Header 4 [package=screwterminal-3.5mm-4_lock]

nets:
  N1: S9.Pin_1, S9.Pin_2, S9.Pin_3, S9.Pin_4, S10.Pin_1, S10.Pin_2, S10.Pin_3, S10.Pin_4, S11.Pin_1, S11.Pin_2, S11.Pin_3, S11.Pin_4, JP7.1, JP7.2, JP7.3, JP7.4
