# Fritzing sketch dc_speed_sens (saved by Fritzing 0.9.3b)
breadboards: 1

parts:
  Part1 = Maker Uno (Arduino Uno Compatible)
  Q1 = NPN-Transistor [package="TO92 [THT]"]
  M2 = fc-51 [package=THT]
  M3 = DC Motor

nets:
  N1: Part1.A0, M2.pin1
  N2: Part1.D6_PWM, Q1.B
  N3: Part1.5V, M2.pin3, M3.pin_2
  N4: Part1.GND, Q1.E, M2.pin2
  N5: Q1.C, M3.pin_1

custom parts:
  Maker Uno (Arduino Uno Compatible): Maker Uno, an Arduino UNO compatible board designed and developed specially for students to learn coding and microcontroller. We named it Maker UNO to encourage everyone to be a maker by getting started with this amazing board. Oh! BTW, it is PURPLE color.
