# Fritzing sketch uno_czujnik (saved by Fritzing 0.9.3b)

parts:
  Part1 = Maker Uno (Arduino Uno Compatible)
  M2 = fc-51 [package=THT]

nets:
  N1: Part1.A0, M2.pin1
  N2: Part1.5V, M2.pin3
  N3: Part1.GND, M2.pin2

custom parts:
  Maker Uno (Arduino Uno Compatible): Maker Uno, an Arduino UNO compatible board designed and developed specially for students to learn coding and microcontroller. We named it Maker UNO to encourage everyone to be a maker by getting started with this amazing board. Oh! BTW, it is PURPLE color.
