# Fritzing sketch uno_dc (saved by Fritzing 0.9.3b)
breadboards: 1

parts:
  Part1 = Maker Uno (Arduino Uno Compatible)
  M3 = DC Motor
  Q1 = NPN-Transistor [package="TO92 [THT]"]

nets:
  N1: Part1.D6_PWM, Q1.B
  N2: Part1.5V, M3.pin_2
  N3: Part1.GND, Q1.E
  N4: M3.pin_1, Q1.C

custom parts:
  Maker Uno (Arduino Uno Compatible): Maker Uno, an Arduino UNO compatible board designed and developed specially for students to learn coding and microcontroller. We named it Maker UNO to encourage everyone to be a maker by getting started with this amazing board. Oh! BTW, it is PURPLE color.
