# Fritzing sketch neopixel_irSensor (saved by Fritzing 0.9.3b)
breadboards: 1

parts:
  Part1 = Maker Uno (Arduino Uno Compatible)
  Part2 = CJMCU2814 [part_number=CJMCU2814]
  IR1 = IR L-73 [package=L-73]

nets:
  N1: Part1.A0, IR1.OUT
  N2: Part1.D6_PWM, Part2.IN
  5V: Part1.5V, Part2.VDD, IR1.VCC
  GND: Part1.GND, Part2.GND, IR1.GND

custom parts:
  Maker Uno (Arduino Uno Compatible): Maker Uno, an Arduino UNO compatible board designed and developed specially for students to learn coding and microcontroller. We named it Maker UNO to encourage everyone to be a maker by getting started with this amazing board. Oh! BTW, it is PURPLE color.
  CJMCU2814: This is the easiest way possible to add small, bright RGB pixels to your project. We took the same technology from our Flora NeoPixels and made them breadboard friendly, with two rows of 3 x 0.1" spaced header on each side for easy soldering, chaining and breadboarding. These ultra-bright LEDs have a constant-current driver cooked right into the LED package! The pixels are chainable - so you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
  IR L-73: Czujnik odbiciowy
