# Fritzing sketch max7219 (saved by Fritzing 0.9.3b)

parts:
  8x8_LED_Modul_mit_MAX1 = 8x8 LED Modul mit MAX7219 [package=THT]
  Part1 = Arduino Leonardo (Rev3b)

nets:
  N1: 8x8_LED_Modul_mit_MAX1.VCC_Eingang, Part1.5V
  N2: 8x8_LED_Modul_mit_MAX1.GND_Eingang, Part1.GND
  N3: 8x8_LED_Modul_mit_MAX1.CS_Eingang, Part1.D9_PWM/A9
