# Fritzing sketch uno_button (saved by Fritzing 0.9.3b)
breadboards: 1

parts:
  Part1 = Maker Uno (Arduino Uno Compatible)
  S7 = Pushbutton [package="[SMD]"]

nets:
  N1: Part1.D13/SCK, S7.Pin_1, S7.Pin_2
  N2: Part1.GND, S7.Pin_3, S7.Pin_4

custom parts:
  Maker Uno (Arduino Uno Compatible): Maker Uno, an Arduino UNO compatible board designed and developed specially for students to learn coding and microcontroller. We named it Maker UNO to encourage everyone to be a maker by getting started with this amazing board. Oh! BTW, it is PURPLE color.
