# Fritzing sketch uno_stepper_button (saved by Fritzing 0.9.3b)
breadboards: 1

parts:
  Part1 = Maker Uno (Arduino Uno Compatible)
  BREAKOUT1 = ULN2003A breakout board
  MOTOR2 = Adafruit Gear-Reduced Stepper Motor (small)  # not connected
  S7 = Pushbutton [package="[SMD]"]

nets:
  N1: Part1.D8, BREAKOUT1.In_1
  N2: Part1.D9_PWM, BREAKOUT1.In_2
  N3: Part1.D10_PWM/SS, BREAKOUT1.In_3
  N4: Part1.D11_PWM/MOSI, BREAKOUT1.In_4
  N5: Part1.D13/SCK, S7.Pin_1, S7.Pin_2
  N6: Part1.GND, BREAKOUT1.0V, S7.Pin_3, S7.Pin_4
  5V: Part1.5V, BREAKOUT1.+5V

custom parts:
  Maker Uno (Arduino Uno Compatible): Maker Uno, an Arduino UNO compatible board designed and developed specially for students to learn coding and microcontroller. We named it Maker UNO to encourage everyone to be a maker by getting started with this amazing board. Oh! BTW, it is PURPLE color.
  ULN2003A breakout board: ULN2003A 7-way Darlington Transistor Driver on breakoutboard
  Adafruit Gear-Reduced Stepper Motor (small): Adafruit gear-reduction stepper motor (small)
