# Fritzing sketch lasery (saved by Fritzing 0.9.3b)

parts:
  Part1 = Maker Uno (Arduino Uno Compatible)
  LED2 = LEDs [package=led10mm]
  M1 = Dagu DGServo 9g (Pan and tilt) [part_number=RS001B]

nets:
  N1: Part1.D11_PWM/MOSI, LED2.A
  GND: Part1.GND, LED2.C, M1.gnd
  N2: Part1.D6_PWM, M1.pulse
  5V: Part1.5V, M1.vcc

notes:
  Laser

custom parts:
  Maker Uno (Arduino Uno Compatible): Maker Uno, an Arduino UNO compatible board designed and developed specially for students to learn coding and microcontroller. We named it Maker UNO to encourage everyone to be a maker by getting started with this amazing board. Oh! BTW, it is PURPLE color.
